# Fritzing sketch hc-sr04 (saved by Fritzing 0.9.2b)
breadboards: 1

parts:
  Mod1 = Raspberry Pi Pico
  Part1 = SRF05 Ultrasonic Rangefinder

nets:
  N1: Mod1.pin_3, Mod1.pin_8, Mod1.pin_13, Mod1.pin_18, Mod1.pin_23, Mod1.pin_28, Mod1.pin_33, Mod1.pin_38, Part1.GND
  N2: Mod1.pin_17, Part1.Echo
  N3: Mod1.pin_19, Part1.Trig
  N4: Mod1.pin_40, Part1.VCC

custom parts:
  Raspberry Pi Pico: Raspberry Pi Pico. Based around the RP2040 microcontroller the Pico is a low cost microcontroller device bringing Raspberry Pi quality, cost, and easy of use to the microcontroller space. Jan 2021, Split part in to two versions: tht (this one) and SMD. This one will drill holes for a .1 in header in pcb to allow plugging in the module as well as providing pads to solder the module to the top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
